# Fritzing sketch brewTimer (saved by Fritzing 0.9.3b)
breadboards: 1

parts:
  Part1 = Arduino Uno (Rev3)
  LCD1 = LCD screen
  R1 = Rotary Potentiometer (Small) [maximum_resistance=100kΩ package=THT]
  R2 = Resistor [tolerance=±5% resistance=220 package=THT]
  S1 = Pushbutton [package="[THT]"]
  S2 = Pushbutton [package="[THT]"]
  S3 = Pushbutton [package="[THT]"]
  S4 = Pushbutton [package="[THT]"]
  S5 = Pushbutton [package="[THT]"]

nets:
  N1: Part1.D8, S5.Pin_1, S5.Pin_2
  N2: Part1.D10_PWM/SS, S4.Pin_3, S4.Pin_4
  N3: Part1.D11_PWM/MOSI, S3.Pin_3, S3.Pin_4
  N4: Part1.D12/MISO, S1.Pin_3, S1.Pin_4
  GND: Part1.GND, LCD1.VSS, LCD1.R/W, LCD1.LED-, R1.leg2
  N5: Part1.D2, LCD1.DB7
  N6: Part1.D3_PWM, LCD1.DB6
  N7: Part1.D4, LCD1.DB5
  N8: Part1.D5_PWM, LCD1.DB4
  N9: Part1.D7, LCD1.RS
  5V: Part1.5V, LCD1.VDD, R1.leg1, R2.Pin_0
  N10: LCD1.V0, R1.wiper
  N11: LCD1.LED+, R2.Pin_1
  N12: S1.Pin_1, S1.Pin_2
  N13: S2.Pin_1, S2.Pin_2
  N14: S2.Pin_3, S2.Pin_4
  N15: S3.Pin_1, S3.Pin_2
  N16: S4.Pin_1, S4.Pin_2
  N17: S5.Pin_3, S5.Pin_4
